# Fritzing sketch circuit (saved by Fritzing 0.9.3b)
breadboards: 1

parts:
  Mojo1 = Embedded Micro Mojo v3
  R2 = TRIMPOT [package=3362u-2]
  U1 = LCD-16X2 [package=lcd-16x2_noholes]
  R3 = Resistor [tolerance=±5% resistance=220 package=THT]

nets:
  GND: Mojo1.GND, R2.CCW, U1.VSS, U1.K
  N1: Mojo1.V+, R2.CW, U1.VDD, R3.Pin_0
  N2: Mojo1.40, U1.DB7
  N3: Mojo1.34, U1.DB6
  N4: Mojo1.32, U1.DB5
  N5: Mojo1.29, U1.DB4
  N6: Mojo1.26, U1.E
  N7: Mojo1.23, U1.R_W
  N8: Mojo1.21, U1.RS
  N9: R2.WIPER, U1.VO
  N10: U1.A, R3.Pin_1

custom parts:
  Embedded Micro Mojo v3: The Mojo is a FPGA development board that is designed from the ground up to be easy to use. The entire goal of the Mojo is to make getting started with FPGA and digital design as easy as possible. To go along with our board, Embedded Micro has tutorials to help you get started and expand your knowledge of digital design. The Mojo is made in the USA. The Mojo features include: Spartan 6 XC6SLX9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
